# Fritzing sketch infra_schema (saved by Fritzing 0.9.3b)
breadboards: 1

parts:
  J1 = Infrared Proximity Sensor
  V1 = DC Power [voltage=5]
  Launchpad1 = TI Launchpad TM4C123GXL

nets:
  N1: J1.Vout, Launchpad1.PD0
  N2: J1.GND, V1.V-
  N3: J1.Vcc, V1.V+
