# Fritzing sketch lm35_schema (saved by Fritzing 0.9.3b)
breadboards: 1

parts:
  V1 = AC Power [voltage=5 frequency=60]
  T1 = LM35 Temperature Sensor [package="TO92 [THT]"]
  Launchpad1 = TI Launchpad TM4C123GXL

nets:
  N1: V1.V+, T1.GND
  N2: V1.V-, T1.+Vs
  N3: T1.Vout, Launchpad1.PD2
