# Fritzing sketch photoresistor_schema (saved by Fritzing 0.9.3b)
breadboards: 1

parts:
  R1 = PHOTOCELL [package=photocell]
  R2 = Resistor [tolerance=±5% resistance=1k package="1206 [SMD]"]
  Launchpad1 = TI Launchpad TM4C123GXL
  Power_Supply = DC Power [voltage=5]

nets:
  N1: R1.P$1, R2.Pin_0, Launchpad1.PD0
  N2: R1.P$2, Power_Supply.V+
  N3: R2.Pin_1, Power_Supply.V-
